// Logisim project exp1-1.circ as structural Verilog: 2 circuits, main circuit main
module main (
  output A,
  output B,
  output Y,
  output halt
);

  wire clock_1_out;

  Counter #(.width(2), .max('h3)) counter_1 (.Q({B, A}), .carry(halt), .clk(clock_1_out));  // open: load, D, count, clr
  Clock clock_1 (.out(clock_1_out));
  \or  or_1 (.A(A), .B(B), .Y(Y));
  LED led_1 (.in(Y));

  // Notes on the sheet:
  //   顶层模块与自制子模块连接部分
  //   本地Logisim验证区域
  //   按Control+K触发执行，再次按Control+K暂停触发
endmodule

module \or  (
  input  A,
  input  B,
  output Y
);

  wire transistor_1_out, transistor_2_out;

  Transistor transistor_1 (.in(1'b1), .out(transistor_1_out), .gate(A));
  Transistor transistor_2 (.in(transistor_1_out), .out(transistor_2_out), .gate(B));
  Transistor #(.\type ("n")) transistor_3 (.in(1'b0), .out(transistor_2_out), .gate(A));
  Transistor #(.\type ("n")) transistor_4 (.in(1'b0), .out(transistor_2_out), .gate(B));
  Transistor transistor_5 (.in(1'b1), .out(Y), .gate(transistor_2_out));
  Transistor #(.\type ("n")) transistor_6 (.in(1'b0), .out(Y), .gate(transistor_2_out));

  // Notes on the sheet:
  //   Q2
  //   Q4
  //   Q1
  //   自制子模块实现区域
  //   Q3
  //   或门实现电路
  //   Q6
  //   Q5
endmodule
