// Logisim project exp1-2 双控开关 - 作答区.circ as structural Verilog: 2 circuits, main circuit main
module main (
  output A,
  output B,
  output Y,
  output halt
);

  wire clock_1_out;

  Counter #(.width(2), .max('h3)) counter_1 (.Q({B, A}), .carry(halt), .clk(clock_1_out));  // open: load, D, count, clr
  Clock clock_1 (.out(clock_1_out));
  \xor  xor_1 (.A(A), .B(B), .Y(Y));
  LED led_1 (.in(Y));

  // Notes on the sheet:
  //   顶层模块与自制子模块连接部分
  //   本地Logisim验证区域
  //   按Control+K触发执行，再次按Control+K暂停触发
endmodule

module \xor  (
  input  A,
  input  B,
  output Y
);

  wire and_1_out, and_2_out, not_1_out, not_2_out;

  not not_1 (not_1_out, A);
  not not_2 (not_2_out, B);
  and and_1 (and_1_out, A, not_2_out);
  and and_2 (and_2_out, not_1_out, B);
  or or_1 (Y, and_1_out, and_2_out);

  // Notes on the sheet:
  //   Q1
  //   Q2
  //   Q3
  //   自制子模块实现区域
  //   Q4
  //   Q5
endmodule
