// Logisim project exp2-2 优先编码器 - 作答区.circ as structural Verilog: 2 circuits, main circuit main
module main (
  output I0,
  output I1,
  output I2,
  output I3,
  output I4,
  output I5,
  output I6,
  output I7,
  output O0,
  output O1,
  output O2,
  output halt
);

  wire clock_1_out;
  wire [3:0] bit_extender_1_out;

  Counter counter_1 (
    .Q({I7, I6, I5, I4, I3, I2, I1, I0}), .carry(halt), .clk(clock_1_out));  // open: load, D, count, clr
  Clock clock_1 (.out(clock_1_out));
  _8_3_pri_encoder u_8_3_pri_encoder_1 (
    .I0(I0), .I1(I1), .O2(O2), .I2(I2), .I3(I3), .I4(I4), .I5(I5), .I6(I6), .I7(I7), .O1(O1), .O0(O0));
  assign bit_extender_1_out = {{1{1'b0}}, {O0, O1, O2}};  // Bit_Extender bit_extender_1
  Hex_Digit_Display hex_digit_display_1 (.value(bit_extender_1_out));  // open: dp

  // Other names for the same wires on the sheet: Y[2:0] = {O0, O1, O2}

  // Notes on the sheet:
  //   顶层模块与自制子模块连接部分
  //   本地Logisim验证区域
  //   按Control+K触发执行，再次按Control+K暂停触发
endmodule

// 8-3 PEncoder
module _8_3_pri_encoder (
  input  I0,
  input  I1,
  input  I2,
  input  I3,
  input  I4,
  input  I5,
  input  I6,
  input  I7,
  output O0,
  output O1,
  output O2
);

  wire and_1_out, and_2_out, and_3_out, and_4_out, and_5_out, and_6_out, and_7_out, not_1_out, not_2_out,
       not_3_out, not_4_out, not_5_out, not_6_out, not_7_out;

  not not_1 (not_1_out, I0);
  not not_2 (not_2_out, I1);
  not not_3 (not_3_out, I2);
  not not_4 (not_4_out, I3);
  not not_5 (not_5_out, I4);
  not not_6 (not_6_out, I5);
  not not_7 (not_7_out, I6);
  and and_1 (and_1_out, not_1_out, I1);
  and and_2 (and_2_out, not_1_out, not_2_out, I2);
  and and_3 (and_3_out, not_1_out, not_2_out, not_3_out, I3);
  and and_4 (and_4_out, not_1_out, not_2_out, not_3_out, not_4_out, I4);
  and and_5 (and_5_out, not_1_out, not_2_out, not_3_out, not_4_out, not_5_out, I5);
  and and_6 (and_6_out, not_1_out, not_2_out, not_3_out, not_4_out, not_5_out, not_6_out, I6);
  and and_7 (and_7_out, not_1_out, not_2_out, not_3_out, not_4_out, not_5_out, not_6_out, not_7_out, I7);
  or or_1 (O0, and_4_out, and_5_out, and_6_out, and_7_out);
  or or_2 (O1, and_2_out, and_3_out, and_6_out, and_7_out);
  or or_3 (O2, and_1_out, and_3_out, and_5_out, and_7_out);

  // Notes on the sheet:
  //   输入信号高电平有效
  //   8-3优先编码器子模块实现区域
  //   （I0）*I1
  //   (I0*I1)*I2
  //   (I0*I1*I2)*I3
  //   (I0***I3)*I4
  //   (I0*****I4)*I5
  //   (I0***I5)*I6
  //   (I0****I6)*I7
  //   高位为O0
  //   低位为O3
endmodule
