// Logisim project exp2-3 选择器级联 - 作答区.circ as structural Verilog: 3 circuits, main circuit main
module main (
  output D0,
  output D1,
  output D2,
  output D3,
  output S0,
  output S1,
  output Y,
  output halt
);

  wire clock_1_out;

  Counter #(.width(6), .max('h3f)) counter_1 (
    .Q({S1, S0, D3, D2, D1, D0}), .carry(halt), .clk(clock_1_out));  // open: load, D, count, clr
  Clock clock_1 (.out(clock_1_out));
  _4_1_mux u_4_1_mux_1 (.D0(D0), .D1(D1), .D2(D2), .D3(D3), .S0(S0), .S1(S1), .Y(Y));
  LED led_1 (.in(Y));

  // Notes on the sheet:
  //   顶层模块与自制子模块连接部分
  //   本地Logisim验证区域
  //   按Control+K触发执行，再次按Control+K暂停触发
endmodule

module _2_1_mux (
  input  A,
  input  B,
  input  S,
  output Y
);

  wire and_1_out, and_2_out;

  and and_1 (and_1_out, A, ~S);  // AND_Gate
  and and_2 (and_2_out, S, B);
  or or_1 (Y, and_1_out, and_2_out);

  // Notes on the sheet:
  //   2选1选择器子模块实现区域
endmodule

module _4_1_mux (
  input  D0,
  input  D1,
  input  D2,
  input  D3,
  input  S0,
  input  S1,
  output Y
);

  wire n2_1_mux_1_y, n2_1_mux_2_y;

  _2_1_mux u_2_1_mux_1 (.A(D0), .B(D1), .Y(n2_1_mux_1_y), .S(S0));
  _2_1_mux u_2_1_mux_2 (.A(D2), .B(D3), .Y(n2_1_mux_2_y), .S(S0));
  _2_1_mux u_2_1_mux_3 (.A(n2_1_mux_1_y), .B(n2_1_mux_2_y), .Y(Y), .S(S1));

  // Notes on the sheet:
  //   低位
  //   高位
  //   4选1选择器子模块实现区域
  //   在其他电路用已经有的分电路的整体为模块的方法
  //   1、在要增加模块的新电路之中进行操作
  //   2、单击要模块化的已经实现好的电路。直接拖拽到要加入模块的电路即可
  //   （其实通过其他的方法可都是可以的，只是是对第二步的重复啦！）
  //   edit circuit layout：展示电路的布局，即咱是通过门电路实现的如何实现的
  //   edit circuit appearance：展示作为模块化（用于其他模块）的样子。即本图中的2-1MUX
  //   analyze circuit：展示此分电路的真值表
  //   get circuit statistics：展示此分电路的信息（基本用不到啦）
endmodule
