// Logisim project exp3-2 加法计数器(v2.7.1) - 作答区.circ as structural Verilog: 3 circuits, main circuit main
module main (
  output Q0,
  output Q1,
  output Q2,
  output Q3,
  output halt
);

  wire clock_1_out, comparator_1_eq;
  wire [7:0] multiplexer_1_out, multiplexer_2_out, multiplexer_3_out, multiplexer_4_out, multiplexer_5_out,
       multiplexer_6_out, multiplexer_7_out, multiplexer_8_out, multiplexer_9_out, multiplexer_10_out,
       multiplexer_11_out, multiplexer_12_out, multiplexer_13_out, multiplexer_14_out, multiplexer_15_out,
       multiplexer_16_out, multiplexer_17_out, multiplexer_18_out, multiplexer_19_out, multiplexer_20_out,
       multiplexer_21_out, multiplexer_22_out, multiplexer_23_out, multiplexer_24_out, multiplexer_25_out,
       multiplexer_26_out;

  Clock clock_1 (.out(clock_1_out));
  Counter #(.width(5), .max('h1f)) counter_1 (.carry(halt), .clk(clock_1_out));  // open: load, D, count, Q, clr
  Multiplexer #(.width(8), .disabled(0), .enable("false")) multiplexer_1 (
    .in1(8'h88), .out(multiplexer_1_out), .sel(comparator_1_eq));  // open: in0
  Multiplexer #(.width(8), .disabled(0), .enable("false")) multiplexer_2 (
    .in1(8'h48), .out(multiplexer_2_out), .sel(comparator_1_eq));  // open: in0
  Multiplexer #(.width(8), .disabled(0), .enable("false")) multiplexer_3 (
    .in1(8'h3f), .out(multiplexer_3_out), .sel(comparator_1_eq));  // open: in0
  Comparator #(.width(4), .mode("unsigned")) comparator_1 (
    .a({Q3, Q2, Q1, Q0}), .b(4'b1111), .eq(comparator_1_eq));  // open: gt, lt
  Multiplexer #(.width(8), .disabled(0), .enable("false")) multiplexer_4 (
    .in1(8'h81), .out(multiplexer_4_out), .sel(comparator_1_eq));  // open: in0
  Multiplexer #(.width(8), .disabled(0), .enable("false")) multiplexer_5 (
    .in1({8{1'b0}}), .out(multiplexer_5_out), .sel(comparator_1_eq));  // open: in0
  Multiplexer #(.width(8), .disabled(0), .enable("false")) multiplexer_6 (
    .in1(8'h3f), .out(multiplexer_6_out), .sel(comparator_1_eq));  // open: in0
  Multiplexer #(.width(8), .disabled(0), .enable("false")) multiplexer_7 (
    .in1(8'h48), .out(multiplexer_7_out), .sel(comparator_1_eq));  // open: in0
  Multiplexer #(.width(8), .disabled(0), .enable("false")) multiplexer_8 (
    .in1({8{1'b1}}), .out(multiplexer_8_out), .sel(comparator_1_eq));  // open: in0
  Multiplexer #(.width(8), .disabled(0), .enable("false")) multiplexer_9 (
    .in1({8{1'b0}}), .out(multiplexer_9_out), .sel(comparator_1_eq));  // open: in0
  Multiplexer #(.width(8), .disabled(0), .enable("false")) multiplexer_10 (
    .in1(8'h81), .out(multiplexer_10_out), .sel(comparator_1_eq));  // open: in0
  Multiplexer #(.width(8), .disabled(0), .enable("false")) multiplexer_11 (
    .in1({8{1'b1}}), .out(multiplexer_11_out), .sel(comparator_1_eq));  // open: in0
  \计数器  \u_计数器_1  (.CLK(clock_1_out), .Q0(Q0), .Q1(Q1), .Q2(Q2), .Q3(Q3));
  DotMatrix #(.matrixcols(26), .matrixrows(8), .persist(1), .dotshape("circle")) dotmatrix_1 (
    .col0(multiplexer_3_out), .col1(multiplexer_2_out), .col2(multiplexer_1_out), .col3(multiplexer_7_out),
    .col4(multiplexer_6_out), .col5(multiplexer_5_out), .col6(multiplexer_4_out), .col7(multiplexer_11_out),
    .col8(multiplexer_10_out), .col9(multiplexer_9_out), .col10(multiplexer_8_out),
    .col11(multiplexer_15_out), .col12(multiplexer_14_out), .col13(multiplexer_13_out),
    .col14(multiplexer_12_out), .col15(multiplexer_19_out), .col16(multiplexer_18_out),
    .col17(multiplexer_17_out), .col18(multiplexer_16_out), .col19(multiplexer_23_out),
    .col20(multiplexer_22_out), .col21(multiplexer_21_out), .col22(multiplexer_20_out),
    .col23(multiplexer_26_out), .col24(multiplexer_25_out), .col25(multiplexer_24_out));
  Multiplexer #(.width(8), .disabled(0), .enable("false")) multiplexer_12 (
    .in1({8{1'b1}}), .out(multiplexer_12_out), .sel(comparator_1_eq));  // open: in0
  Multiplexer #(.width(8), .disabled(0), .enable("false")) multiplexer_13 (
    .in1(8'h7), .out(multiplexer_13_out), .sel(comparator_1_eq));  // open: in0
  Multiplexer #(.width(8), .disabled(0), .enable("false")) multiplexer_14 (
    .in1(8'h3c), .out(multiplexer_14_out), .sel(comparator_1_eq));  // open: in0
  Multiplexer #(.width(8), .disabled(0), .enable("false")) multiplexer_15 (
    .in1(8'he0), .out(multiplexer_15_out), .sel(comparator_1_eq));  // open: in0
  Multiplexer #(.width(8), .disabled(0), .enable("false")) multiplexer_16 (
    .in1(8'h3), .out(multiplexer_16_out), .sel(comparator_1_eq));  // open: in0
  Multiplexer #(.width(8), .disabled(0), .enable("false")) multiplexer_17 (
    .in1(8'h1), .out(multiplexer_17_out), .sel(comparator_1_eq));  // open: in0
  Multiplexer #(.width(8), .disabled(0), .enable("false")) multiplexer_18 (
    .in1(8'h1), .out(multiplexer_18_out), .sel(comparator_1_eq));  // open: in0
  Multiplexer #(.width(8), .disabled(0), .enable("false")) multiplexer_19 (
    .in1({8{1'b0}}), .out(multiplexer_19_out), .sel(comparator_1_eq));  // open: in0
  Hex_Digit_Display hex_digit_display_1 (.value({Q3, Q2, Q1, Q0}));  // open: dp
  Multiplexer #(.width(8), .disabled(0), .enable("false")) multiplexer_20 (
    .in1(8'h1), .out(multiplexer_20_out), .sel(comparator_1_eq));  // open: in0
  Multiplexer #(.width(8), .disabled(0), .enable("false")) multiplexer_21 (
    .in1(8'hfe), .out(multiplexer_21_out), .sel(comparator_1_eq));  // open: in0
  Multiplexer #(.width(8), .disabled(0), .enable("false")) multiplexer_22 (
    .in1({8{1'b0}}), .out(multiplexer_22_out), .sel(comparator_1_eq));  // open: in0
  Multiplexer #(.width(8), .disabled(0), .enable("false")) multiplexer_23 (
    .in1(8'hfe), .out(multiplexer_23_out), .sel(comparator_1_eq));  // open: in0
  Multiplexer #(.width(8), .disabled(0), .enable("false")) multiplexer_24 (
    .in1(8'hfe), .out(multiplexer_24_out), .sel(comparator_1_eq));  // open: in0
  Multiplexer #(.width(8), .disabled(0), .enable("false")) multiplexer_25 (
    .in1(8'h1), .out(multiplexer_25_out), .sel(comparator_1_eq));  // open: in0
  Multiplexer #(.width(8), .disabled(0), .enable("false")) multiplexer_26 (
    .in1(8'h1), .out(multiplexer_26_out), .sel(comparator_1_eq));  // open: in0

  // Other names for the same wires on the sheet: Count[3:0] = {Q3, Q2, Q1, Q0}

  // Notes on the sheet:
  //   顶层模块与自制子模块连接部分
  //   本地Logisim验证区域
  //   按Control+K触发执行，再次按Control+K暂停触发
endmodule

module T_flipflop (
  input  T,
  output Q,
  output QN
);

  D_Flip_Flop d_ff_1 (.clk(T), .D(QN), .Q(Q), .Qn(QN));  // open: preset, en, reset

  // Notes on the sheet:
  //   T触发器子模块实现区域
endmodule

module \计数器  (
  input  CLK,
  output Q0,
  output Q1,
  output Q2,
  output Q3
);

  wire t_flipflop_1_qn, t_flipflop_2_qn, t_flipflop_3_qn;

  T_flipflop t_flipflop_1 (.T(CLK), .Q(Q0), .QN(t_flipflop_1_qn));
  T_flipflop t_flipflop_2 (.T(t_flipflop_1_qn), .Q(Q1), .QN(t_flipflop_2_qn));
  T_flipflop t_flipflop_3 (.T(t_flipflop_2_qn), .Q(Q2), .QN(t_flipflop_3_qn));
  T_flipflop t_flipflop_4 (.T(t_flipflop_3_qn), .Q(Q3));  // open: QN

  // Notes on the sheet:
  //   计数器子模块实现区域
  //   规则：加上一个数。每次Q0都会发生改变》》把Q0放在第一个T触发之中
  //   根据加法的规则，只有前面低位的全是1了，才能对后面高位的进行改变。》》Qn作为后面T触发的时钟信号
  //   输出信号为Q0\Q1\Q2\Q3
  //   高位是Q3 最低位是Q0
  //   即接收信号为Q0Q1Q2Q3
endmodule
