// Logisim project exp3-3 移位寄存器(v2.7.1) - 作答区.circ as structural Verilog: 2 circuits, main circuit main
module main (
  output CLK,
  output CLR,
  output LIN,
  output RIN,
  output S1,
  output S0,
  output A,
  output B,
  output C,
  output D,
  output QA,
  output QB,
  output QC,
  output QD,
  output halt
);

  wire [3:0] bit_extender_1_out;
  wire [4:0] counter_1_q;
  wire [15:9] rom_1_data;

  Clock clock_1 (.out(CLK));
  Counter #(.width(5), .max('h1f)) counter_1 (.Q(counter_1_q), .carry(halt), .clk(CLK));  // open: load, D, count, clr
  Bit_Extender #(.in_width(5), .out_width(4)) bit_extender_1 (.in(counter_1_q), .out(bit_extender_1_out));
  ROM #(.addrWidth(4), .dataWidth(16)) rom_1 (
    .addr(bit_extender_1_out), .data({rom_1_data, CLR, LIN, RIN, S1, S0, A, B, C, D}));  // open: sel
  \_4位移位寄存器  \u_4位移位寄存器_1  (
    .CLK(CLK), .CLR(CLR), .LIN(LIN), .RIN(RIN), .S1(S1), .S0(S0), .D(D), .C(C), .B(B), .A(A), .QD(QD),
    .QC(QC), .QB(QB), .QA(QA));
  DotMatrix #(.matrixcols(4), .matrixrows(1)) dotmatrix_1 (.col0(QA), .col1(QB), .col2(QC), .col3(QD));

  // Other names for the same wires on the sheet: A_t = QA; B_t = QB; C_t = QC; D_t = QD

  // Notes on the sheet:
  //   contents of rom_1 (hex, n*v repeats v):
  //   100 35 5f 50 55 5a 90 1f 15f 3a af a0 a5 aa 60 2f
  //   顶层模块与自制子模块连接部分
  //   本地Logisim验证区域
  //   按Control+K触发执行，再次按Control+K暂停触发
  //   实现的功能：数据左移、数据右移、数据保持、数据载入
endmodule

module \_4位移位寄存器  (
  input  CLK,
  input  CLR,
  input  LIN,
  input  RIN,
  input  S1,
  input  S0,
  input  D,
  input  C,
  input  B,
  input  A,
  output QD,
  output QC,
  output QB,
  output QA
);

  wire _00_2_out, _00_3_out, _00_4_out, _00_out, \_01_右_2_out , \_01_右_3_out , \_01_右_4_out , \_01_右_out ,
       \_10_左_2_out , \_10_左_3_out , \_10_左_4_out , \_10_左_out , _11_2_out, _11_3_out, _11_4_out, _11_out,
       not_1_out, not_2_out, not_3_out, or_1_out, or_2_out, or_3_out, or_4_out;

  not not_1 (not_1_out, CLR);
  not not_2 (not_2_out, S1);
  not not_3 (not_3_out, S0);
  and \_10_左  (\_10_左_out , not_1_out, S1, not_3_out, LIN);
  and _00 (_00_out, not_1_out, not_2_out, not_3_out, QD);
  and _11 (_11_out, not_1_out, S1, S0, D);
  and \_01_右  (\_01_右_out , not_1_out, not_2_out, S0, QC);
  and \_10_左_2  (\_10_左_2_out , not_1_out, S1, not_3_out, QD);
  and _00_2 (_00_2_out, not_1_out, not_2_out, not_3_out, QC);
  and _11_2 (_11_2_out, not_1_out, S1, S0, C);
  and \_01_右_2  (\_01_右_2_out , not_1_out, not_2_out, S0, QB);
  and \_10_左_3  (\_10_左_3_out , not_1_out, S1, not_3_out, QC);
  and _00_3 (_00_3_out, not_1_out, not_2_out, not_3_out, QB);
  and _11_3 (_11_3_out, not_1_out, S1, S0, B);
  and \_01_右_3  (\_01_右_3_out , not_1_out, not_2_out, S0, QA);
  and \_10_左_4  (\_10_左_4_out , not_1_out, S1, not_3_out, QB);
  and _00_4 (_00_4_out, not_1_out, not_2_out, not_3_out, QA);
  and _11_4 (_11_4_out, not_1_out, S1, S0, A);
  and \_01_右_4  (\_01_右_4_out , not_1_out, not_2_out, S0, RIN);
  or or_1 (or_1_out, \_10_左_out , _00_out, _11_out, \_01_右_out );
  or or_2 (or_2_out, \_10_左_2_out , _00_2_out, _11_2_out, \_01_右_2_out );
  or or_3 (or_3_out, \_10_左_3_out , _00_3_out, _11_3_out, \_01_右_3_out );
  or or_4 (or_4_out, \_10_左_4_out , _00_4_out, _11_4_out, \_01_右_4_out );
  D_Flip_Flop #(.trigger("falling")) d_ff_1 (.clk(CLK), .D(or_1_out), .Q(QD));  // open: Qn, preset, en, reset
  D_Flip_Flop #(.trigger("falling")) d_ff_2 (.clk(CLK), .D(or_2_out), .Q(QC));  // open: Qn, preset, en, reset
  D_Flip_Flop #(.trigger("falling")) d_ff_3 (.clk(CLK), .D(or_3_out), .Q(QB));  // open: Qn, preset, en, reset
  D_Flip_Flop #(.trigger("falling")) d_ff_4 (.clk(CLK), .D(or_4_out), .Q(QA));  // open: Qn, preset, en, reset

  // Notes on the sheet:
  //   外部清0信号。CLR=1
  //   让QAQBQCQD全都为0
  //   让QA=A QD=D
  //   SO=S1=0数据保持
  //   S0=1\S1=0数据左移
  //   S0=0\S1=1数据右移
  //   S0=S1=1数据载入
  //   4位移位寄存器子模块实现区域
  //   数据右移动--S1=0 S0=1
  //   输出的顺序QA QB QC QD
  //   左移的时候。顶掉了QA
  //   右移的时候。顶掉了QD
  //   移位的时候，QA为最左端。QB为最右端
  //   右移操作的时候，左端补上新输入的RIN
  //   左移操作的时候，右端补上新输入的LIN
endmodule
