// Logisim project exp4-2 级联加法器(v2.7.1) - 作答区.circ as structural Verilog: 6 circuits, main circuit main
module main (
  output Cin,
  output [15:0] X,
  output halt,
  output [15:0] Y,
  output Cout,
  output [15:0] S
);

  wire [3:0] bit_extender_1_out, counter_1_q;

  Clock clock_1 (.out(Cin));
  Counter #(.width(4), .max('hf), .trigger("falling")) counter_1 (
    .Q(counter_1_q), .carry(halt), .clk(Cin));  // open: load, D, count, clr
  assign bit_extender_1_out = {{3{1'b0}}, Cin};  // Bit_Extender bit_extender_1
  ROM #(.addrWidth(4), .dataWidth(16)) rom_1 (.addr(counter_1_q), .data(X));  // open: sel
  ROM #(.addrWidth(4), .dataWidth(16)) rom_2 (.addr(counter_1_q), .data(Y));  // open: sel
  Hex_Digit_Display hex_digit_display_1 (.value(bit_extender_1_out));  // open: dp
  Hex_Digit_Display hex_digit_display_2 (.value(S[15:12]));  // open: dp
  Hex_Digit_Display hex_digit_display_3 (.value(X[15:12]));  // open: dp
  Hex_Digit_Display hex_digit_display_4 (.value(X[11:8]));  // open: dp
  Hex_Digit_Display hex_digit_display_5 (.value(S[11:8]));  // open: dp
  Hex_Digit_Display hex_digit_display_6 (.value(S[7:4]));  // open: dp
  Hex_Digit_Display hex_digit_display_7 (.value(X[3:0]));  // open: dp
  Hex_Digit_Display hex_digit_display_8 (.value(X[7:4]));  // open: dp
  Hex_Digit_Display hex_digit_display_9 (.value(S[3:0]));  // open: dp
  \_16位CLA  \u_16位cla_1  (
    .Cin(Cin), .X1(X[3:0]), .Y1(Y[3:0]), .X2(X[7:4]), .Y2(Y[7:4]), .X3(X[11:8]), .Y3(Y[11:8]), .X4(X[15:12]),
    .Y4(Y[15:12]), .S1(S[3:0]), .S2(S[7:4]), .S3(S[11:8]), .S4(S[15:12]), .Cout(Cout));
  Hex_Digit_Display hex_digit_display_10 (.value(Y[15:12]));  // open: dp
  LED led_1 (.in(Cout));
  Hex_Digit_Display hex_digit_display_11 (.value(Y[7:4]));  // open: dp
  Hex_Digit_Display hex_digit_display_12 (.value(Y[11:8]));  // open: dp
  Hex_Digit_Display hex_digit_display_13 (.value(Y[3:0]));  // open: dp

  // Notes on the sheet:
  //   =
  //   contents of rom_1 (hex, n*v repeats v):
  //   0 1111 2222 3333 4444 5555 6666 7777 8888 9999 a00a b00b c00c d00d eeee ffff
  //   contents of rom_2 (hex, n*v repeats v):
  //   aaaa ffff 101 202 303 a0a b0b c0c d0d f0f eeee dddd cccc bbbb 1 1
  //   +
  //   Cin
  //   S1
  //   X1
  //   X1
  //   S2
  //   S3
  //   顶层模块与自制子模块连接部分
  //   本地Logisim验证区域
  //   按Control+K触发执行，再次按Control+K暂停触发
  //   X1
  //   X1
  //   S4
  //   Y1
  //   +
  //   Cout
  //   Y3
  //   Y2
  //   Y4
endmodule

// FA
module \_1位全加器  (
  input  Cin,
  input  X,
  input  Y,
  output F,
  output P,
  output G
);


  // Notes on the sheet:
  //   全加法器子模块实现区域
endmodule

// 4-bit CLU
module \_4位CLU  (
  input  C0,
  input  P1,
  input  G1,
  input  P2,
  input  G2,
  input  P3,
  input  G3,
  input  P4,
  input  G4,
  output C1,
  output C2,
  output C3,
  output C4
);


  // Notes on the sheet:
  //   先行进位逻辑单元子模块实现区域
endmodule

// 组间进位函数逻辑
module \组间进位函数逻辑单元  (
  input  P1,
  input  G1,
  input  P2,
  input  G2,
  input  P3,
  input  G3,
  input  P4,
  input  G4,
  output Pg,
  output Gg
);


  // Notes on the sheet:
  //   组间进位函数逻辑单元子模块实现区域
endmodule

// 4-bit CLA
module \可级联的4位CLA  (
  input  Cin,
  input  [3:0] X,
  input  [3:0] Y,
  output Pg,
  output Gg,
  output [3:0] S,
  output Cout
);


  // Notes on the sheet:
  //   先行进位加法器子模块实现区域
endmodule

// 16-bit CLA
module \_16位CLA  (
  input  Cin,
  input  [3:0] X1,
  input  [3:0] Y1,
  input  [3:0] X2,
  input  [3:0] Y2,
  input  [3:0] X3,
  input  [3:0] Y3,
  input  [3:0] X4,
  input  [3:0] Y4,
  output [3:0] S1,
  output [3:0] S2,
  output [3:0] S3,
  output [3:0] S4,
  output Cout
);


  // Notes on the sheet:
  //   16位级联先行进位加法器子模块实现区域
endmodule
