// Logisim project exp4-3 算术逻辑部件(v2.7.1) - 作答区.circ as structural Verilog: 4 circuits, main circuit main
module main (
  output [3:0] ALUctr,
  output [3:0] X,
  output [3:0] Y,
  output Zero,
  output [3:0] Result,
  output halt
);

  wire clk, comparator_1_eq, not_1_out;
  wire [3:0] counter_1_q, counter_2_q, rom_4_data;

  Clock clock_1 (.out(clk));
  Counter #(.width(4), .max('hf), .trigger("falling")) counter_1 (
    .Q(counter_1_q), .carry(halt), .clk(clk));  // open: load, D, count, clr
  // Probe on ALUctr
  Hex_Digit_Display hex_digit_display_1 (.value(X));  // open: dp
  Hex_Digit_Display hex_digit_display_2 (.value(Y));  // open: dp
  ROM #(.addrWidth(4), .dataWidth(4)) rom_1 (.addr(counter_1_q), .data(ALUctr));  // open: sel
  ROM #(.addrWidth(4), .dataWidth(4)) rom_2 (.addr(counter_1_q), .data(X));  // open: sel
  ROM #(.addrWidth(4), .dataWidth(4)) rom_3 (.addr(counter_1_q), .data(Y));  // open: sel
  Hex_Digit_Display hex_digit_display_3 (.value(Result));  // open: dp
  LED led_1 (.in(Zero));
  Counter #(.width(4), .max('hf), .trigger("falling")) counter_2 (
    .Q(counter_2_q), .clk(clk));  // open: load, D, count, carry, clr
  \算术逻辑部件_ALU  \u_算术逻辑部件_alu_1  (.X(X), .Y(Y), .ALUctr(ALUctr), .Zero(Zero), .Result(Result));
  ROM #(.addrWidth(4), .dataWidth(4)) rom_4 (.addr(counter_2_q), .data(rom_4_data));  // open: sel
  Comparator #(.width(4), .mode("unsigned")) comparator_1 (
    .a(rom_4_data), .b(Result), .eq(comparator_1_eq));  // open: gt, lt
  not not_1 (not_1_out, comparator_1_eq);
  RAM #(.addrWidth(4), .dataWidth(16), .bus("separate")) ram_1 (
    .addr(counter_2_q), .din({counter_2_q, ALUctr, X, Y}), .str(not_1_out), .clk(clk));  // open: data, sel, ld, clr

  // Notes on the sheet:
  //   ALUctr
  //   操作数X
  //   操作数Y
  //   contents of rom_1 (hex, n*v repeats v):
  //   0 0 0 2 2 2 3 3 3 6 6 6 8 8 8 f
  //   contents of rom_2 (hex, n*v repeats v):
  //   1 a f 3 3 0 3 3 a f 0 a f 3 1 3
  //   contents of rom_3 (hex, n*v repeats v):
  //   2 a 1 7 8 a 7 8 8 0 5 9 1 3 3 5
  //   Result
  //   Zero
  //   顶层模块与自制子模块连接部分
  //   本地Logisim验证区域
  //   按Control+K触发执行，再次按Control+K暂停触发
  //   错误记录
  //   contents of rom_4 (hex, n*v repeats v):
  //   3 4 0 1 0 0 1 1 0 f 5 b e 0 e 5
  //   记录每个条目为16bits：
  //   最高4位为指令index，
  //   次高4位为ALUctr，
  //   次低4位为操作数X，
  //   最低4位为操作数Y。
endmodule

// 4-bit adder
module \_4位带标志位加法器  (
  input  Cin,
  input  X1,
  input  Y1,
  input  X2,
  input  Y2,
  input  X3,
  input  Y3,
  input  X4,
  input  Y4,
  output Cout,
  output OF,
  output SF,
  output ZF,
  output CF,
  output S1,
  output S2,
  output S3,
  output S4
);

  wire adder_1_cout, adder_2_cout, adder_3_cout;

  Adder #(.width(1)) adder_1 (.a(X1), .b(Y1), .out(S1), .cin(Cin), .cout(adder_1_cout));
  Adder #(.width(1)) adder_2 (.a(X2), .b(Y2), .out(S2), .cin(adder_1_cout), .cout(adder_2_cout));
  Adder #(.width(1)) adder_3 (.a(X3), .b(Y3), .out(S3), .cin(adder_2_cout), .cout(adder_3_cout));
  Adder #(.width(1)) adder_4 (.a(X4), .b(Y4), .out(S4), .cin(adder_3_cout), .cout(Cout));
  xor u_OF (OF, adder_3_cout, Cout);
  xor u_CF (CF, Cin, Cout);
  nor nor_1 (ZF, S1, S2, S3, S4);

  assign SF = S4;

  // Notes on the sheet:
  //   两个数X4X3X2X1和Y4Y3Y2Y1（高-低）
  //   错误：没有调整加法器中的bite数量
  //   logisim中的adder是一个提供任意输入位数的一个加法器
  //   而不是一个半成品“全加器”
  //   而如果是bite为1的时候，加法器就降为了全加器了！
  //   带标志位加法器子模块实现区域
  //   高位进位
  //   溢出
  //   符号
  //   零标志
  //   进位、借位标志
  //   Si分别是Xi+Yi的结果
endmodule

module \ALU操作控制信号生成部件  (
  input  [3:0] ALUctr,
  output SUBctr,
  output SIGctr,
  output OPctr0,
  output OPctr1
);

  wire and_1_out, and_2_out, and_3_out, not_2_out, not_3_out;

  not not_1 (SIGctr, ALUctr[0]);
  not not_2 (not_2_out, ALUctr[2]);
  not not_3 (not_3_out, ALUctr[3]);
  and and_1 (and_1_out, ALUctr[1], not_2_out, not_3_out);
  and and_2 (and_2_out, SIGctr, ALUctr[1], ALUctr[2], not_3_out);
  and and_3 (and_3_out, ALUctr[0], ALUctr[1], ALUctr[2], ALUctr[3]);
  or or_1 (SUBctr, ALUctr[3], and_1_out);
  or or_2 (OPctr0, and_1_out, and_2_out);
  or or_3 (OPctr1, and_1_out, and_3_out);

  // Notes on the sheet:
  //   ALU操作控制信号生成子模块实现区域
endmodule

// ALU
module \算术逻辑部件_ALU  (
  input  [3:0] X,
  input  [3:0] Y,
  input  [3:0] ALUctr,
  output Zero,
  output [3:0] Result
);

  wire \alu操作控制信号生成部件_1_opctr0 , \alu操作控制信号生成部件_1_opctr1 , \alu操作控制信号生成部件_1_sigctr ,
       \alu操作控制信号生成部件_1_subctr , Cin_cf, Cin_of, Cin_sf, multiplexer_5_out, not_2_out, xor_1_out, xor_2_out;
  wire [3:0] bit_extender_1_out, Cin_s1, multiplexer_1_out, multiplexer_2_out, multiplexer_3_out, not_1_out,
       or_1_out;

  assign not_1_out = ~Y;  // NOT_Gate not_1, 4 bits wide
  Multiplexer #(.width(4), .enable("false")) multiplexer_1 (
    .in0(Y), .in1(not_1_out), .out(multiplexer_1_out), .sel(\alu操作控制信号生成部件_1_subctr ));
  \_4位带标志位加法器  Cin (
    .X1(X[0]), .S1(Cin_s1[0]), .S2(Cin_s1[1]), .S3(Cin_s1[2]), .S4(Cin_s1[3]), .Y1(multiplexer_1_out[0]),
    .X2(X[1]), .Y2(multiplexer_1_out[1]), .X3(X[2]), .Y3(multiplexer_1_out[2]), .X4(X[3]),
    .Y4(multiplexer_1_out[3]), .Cin(\alu操作控制信号生成部件_1_subctr ), .SF(Cin_sf), .ZF(Zero), .CF(Cin_cf),
    .OF(Cin_of));  // open: Cout
  assign or_1_out = X | Y;  // OR_Gate or_1, 4 bits wide
  assign bit_extender_1_out = {{3{1'b0}}, multiplexer_5_out};  // Bit_Extender bit_extender_1
  \ALU操作控制信号生成部件  \alu操作控制信号生成部件_1  (
    .ALUctr(ALUctr), .SUBctr(\alu操作控制信号生成部件_1_subctr ), .SIGctr(\alu操作控制信号生成部件_1_sigctr ),
    .OPctr0(\alu操作控制信号生成部件_1_opctr0 ), .OPctr1(\alu操作控制信号生成部件_1_opctr1 ));
  not not_2 (not_2_out, Cin_cf);
  Multiplexer #(.width(4), .enable("false")) multiplexer_2 (
    .in0(Cin_s1), .in1(Y), .out(multiplexer_2_out), .sel(\alu操作控制信号生成部件_1_opctr1 ));
  Multiplexer #(.width(4), .enable("false")) multiplexer_3 (
    .in0(or_1_out), .in1(bit_extender_1_out), .out(multiplexer_3_out), .sel(\alu操作控制信号生成部件_1_opctr1 ));
  Multiplexer #(.width(4), .enable("false")) multiplexer_4 (
    .in0(multiplexer_2_out), .in1(multiplexer_3_out), .out(Result), .sel(\alu操作控制信号生成部件_1_opctr0 ));
  xor xor_1 (xor_1_out, \alu操作控制信号生成部件_1_subctr , not_2_out);
  xor xor_2 (xor_2_out, Cin_sf, Cin_of);
  Multiplexer #(.enable("false")) multiplexer_5 (
    .in0(xor_1_out), .in1(xor_2_out), .out(multiplexer_5_out), .sel(\alu操作控制信号生成部件_1_sigctr ));

  // Notes on the sheet:
  //   4位输入
  //   4位输入
  //          操作控制信号
  //                            和PPT中ALUop的含义一样
  //   ALUop在子电路实现的时候已经加了spliter了
  //   算术逻辑部件子模块实现区域
  //   分离器splitter的逆用！(现在可能方向有问题)
  //   4位的输出
  //   4种标志位
  //   上-下：ST\ZF\CF\OF
  //   00
  //   10
  //   01
  //   11
  //   操作控制信号的具体含义--功能选择：
  //   1、选择【加法add】（此时SUBctr=0.OPctr10=00.没有SIG）
  //   2、选择【有符号整数减法slt】SUBctr=1、SIGctr=1.OPctr10=11
  //   3、选择【无符号整数比较大小】SUB=1.SIG=0    OP10=11
  //   4、选择【按照每一位进行“或”OP=01.没有SUB.SIG】
  //   5、选择【加法器的结果进行输出（Cin=1，做的减法）SUB=1.没有SIG.OP】
  //   6、选择【操作数B直接输出】OP=10没有SUB.SIG
  //   Cin为0的时候为加。
  //   以下两种x<y时候输出1
  //   CF-进位、借位信号（无符号）
  //   OF-溢出信号（有符号）
  //   SF-符号标志
  //   无符号数比较大小Cin异或~CF
  //   有符号数比较大小 OF异或SF
endmodule
